# Fritzing sketch wiring (saved by Fritzing 0.9.2b)
breadboards: 1

parts:
  M2 = DC Motor
  M3 = DC Motor
  M4 = DC Motor
  IC1 = L293D [package=THT]
  U1 = atmega328 [package=dip]
  IC2 = L293D [package=THT]
  EC_Sensor = TMP36 [package=to-92]
  pH_Sensor = TMP36 [package=to-92]  # not connected
  U2 = RELAY [package=relay-g5q]  # not connected

nets:
  N1: M2.pin_1, IC1.Out_2_(_Controlled_by_Enable_1_)
  N2: M2.pin_2, IC1.Out_1_(_Controlled_by_Enable_1_)
  N3: M3.pin_1, IC2.Out_2_(_Controlled_by_Enable_1_)
  N4: M3.pin_2, IC2.Out_1_(_Controlled_by_Enable_1_)
  N5: M4.pin_1, IC1.Out_4_(_Controlled_by_Enable_2_)
  N6: M4.pin_2, IC1.Out_3_(_Controlled_by_Enable_2_)
  N7: IC1.In_1, U1.D3_(PWM)
  N8: IC1.In_2, U1.D2
  N9: IC1.In_3, U1.VCC
  N10: IC1.In_4, U1.D4
  N11: U1.GND, IC2.In_2
  N12: U1.D5_(PWM), IC2.In_1
  N13: U1.A1, EC_Sensor.VOUT

notes:
  Dosing Unit
